// Logisim project hw4.circ as structural Verilog: 1 circuit, main circuit main
module main (
  input  X,
  output Z
);

  wire and_1_out, and_2_out, and_3_out, and_4_out, and_5_out, and_6_out, and_7_out, and_8_out, and_9_out,
       and_10_out, button_1_out, clock_1_out, S0_prime_out, S0_q, S1_prime_out, S1_q, S2_prime_out, S2_q;

  Clock clock_1 (.out(clock_1_out));
  Button button_1 (.out(button_1_out));
  D_Flip_Flop S2 (.clk(clock_1_out), .D(S2_prime_out), .Q(S2_q), .reset(button_1_out));  // open: Qn, preset, en
  and and_1 (and_1_out, ~S2_q, S1_q, ~X);  // AND_Gate
  and and_2 (and_2_out, S2_q, ~S0_q, X);  // AND_Gate
  and and_3 (and_3_out, ~S2_q, S1_q);  // AND_Gate
  and and_4 (and_4_out, S1_q, ~S0_q);  // AND_Gate
  and and_5 (and_5_out, ~S1_q, X);  // AND_Gate
  and and_6 (and_6_out, ~S1_q, S0_q);  // AND_Gate
  and and_7 (and_7_out, S2_q, X);
  and and_8 (and_8_out, S2_q, S0_q);
  and and_9 (and_9_out, ~S2_q, S1_q, ~S0_q, ~X);  // AND_Gate
  and and_10 (and_10_out, S1_q, S0_q, X);
  or S2_prime (S2_prime_out, and_1_out, and_2_out);
  or S1_prime (S1_prime_out, ~X, and_3_out, and_4_out);  // OR_Gate
  or S0_prime (S0_prime_out, and_5_out, and_6_out, and_7_out, and_8_out);
  or u_Z (Z, and_9_out, and_10_out);
  D_Flip_Flop S1 (.clk(clock_1_out), .D(S1_prime_out), .Q(S1_q), .reset(button_1_out));  // open: Qn, preset, en
  D_Flip_Flop S0 (.clk(clock_1_out), .D(S0_prime_out), .Q(S0_q), .reset(button_1_out));  // open: Qn, preset, en
endmodule
